# Fritzing sketch Capstone_scarecrowbot_eric_buhr (saved by Fritzing 0.9.3b)
breadboards: 1

parts:
  Part1 = Spark Core (v1.0)
  J1 = Piezo Speaker
  R1 = Resistor [tolerance=±5% resistance=220 package=THT]
  LED1 = LED - 5mm [color="Red (633nm)" package="5 mm [THT]"]
  U1 = MLX90614 [package=to-39]  # not connected

nets:
  N1: Part1.TX, J1.pin2
  N2: Part1.D1, J1.pin1, R1.Pin_0
  N3: R1.Pin_1, LED1.anode
